// Logisim project 8-bit-cpu.circ as structural Verilog: 6 circuits, main circuit 8 bit register
module main (
  input  in_1,
  input  in_2,
  input  in_3,
  input  in_4,
  input  in_5,
  input  in_6,
  input  in_7,
  input  in_8,
  input  in_9,
  input  in_10
);

  wire A_r0, A_r1, A_r2, A_r3, A_r4, A_r5, A_r6, A_r7, ALU_out_20, ALU_out_21, ALU_out_22, ALU_out_23,
       ALU_out_24, ALU_out_25, ALU_out_26, ALU_out_27, ALU_out_37, ALUO, ALUS, B_r0, B_r1, B_r2, B_r3, B_r4,
       B_r5, B_r6, B_r7, CF, clock_1_out, clock_2_out, clock_3_out, clock_4_out, clock_5_out, clock_6_out,
       clock_7_out, clock_8_out, clock_9_out, Current_instruction_register_r0,
       Current_instruction_register_r1, Current_instruction_register_r2, Current_instruction_register_r3, FL,
       IRLD, IRO, LDA, LDB, MA_Register_out_17, MA_Register_r0, MA_Register_r1, MA_Register_r2,
       MA_Register_r3, MALD, MAO, MCC, not_1_out, O1, O2, O3, O4, O5, O6, O7, O8, OEA, OEB, or_1_out, ORLD,
       PC_out_14, PC_out_15, PC_out_16, PC_out_17, PCC, PCLD, PCO, ram_1_out_25, ram_1_out_26, ram_1_out_27,
       ram_1_out_28, ram_1_out_29, ram_1_out_30, ram_1_out_31, ram_1_out_32, RAMO, RAMW, ZF;
  wire [1:0] ALU_out_36;
  wire [7:0] microcounter_1_out_3;
  wire [23:18] rom_1_data;

  Register #(.width(2)) register_1 (.D(ALU_out_36), .en(FL), .Q({ZF, CF}), .clk(clock_1_out), .clr(in_2));
  Clock clock_1 (.out(clock_1_out));
  LED led_1 (.in(ALU_out_37));
  LED led_2 (.in(O2));
  LED led_3 (.in(O1));
  LED led_4 (.in(O3));
  LED led_5 (.in(O5));
  LED led_6 (.in(O7));
  LED led_7 (.in(O4));
  LED led_8 (.in(O6));
  LED led_9 (.in(O8));
  alu ALU (
    .in_1(A_r0), .in_2(A_r1), .in_3(A_r2), .in_4(A_r3), .in_5(A_r4), .in_6(A_r5), .in_7(A_r6), .in_8(A_r7),
    .in_9(B_r0), .in_10(B_r1), .in_12(B_r2), .in_13(B_r3), .in_14(B_r4), .in_15(B_r5), .in_16(B_r6),
    .in_17(ALUS), .out_28(in_10), .out_29(in_9), .out_30(in_8), .out_31(in_7), .out_32(in_6), .out_33(in_5),
    .out_34(in_4), .out_35(in_3), .out_20(ALU_out_20), .out_21(ALU_out_21), .out_22(ALU_out_22),
    .out_23(ALU_out_23), .out_24(ALU_out_24), .out_25(ALU_out_25), .out_26(ALU_out_26), .out_27(ALU_out_27),
    .out_36(ALU_out_36[0]), .out_37(ALU_out_37), .in_11(ALUO), .in_18(B_r7), .out_19(ALU_out_36[1]));
  Clock clock_2 (.out(clock_2_out));
  Clock clock_3 (.out(clock_3_out));
  ROM #(.addrWidth(10), .dataWidth(24)) rom_1 (
    .addr({CF, ZF, microcounter_1_out_3}),
    .data({rom_1_data, ORLD, FL, OEA, LDA, OEB, LDB, ALUO, ALUS, PCLD, PCO, PCC, MAO, MALD, RAMO, RAMW, IRO, IRLD, MCC}),
    .sel(1'b1));
  LED led_10 (.in(A_r5));
  LED led_11 (.in(A_r6));
  LED led_12 (.in(A_r7));
  LED led_13 (.in(A_r4));
  LED led_14 (.in(ALU_out_21));
  LED led_15 (.in(ALU_out_23));
  LED led_16 (.in(ALU_out_22));
  LED led_17 (.in(ALU_out_20));
  LED led_18 (.in(B_r5));
  LED led_19 (.in(B_r4));
  LED led_20 (.in(B_r6));
  LED led_21 (.in(B_r7));
  microcounter microcounter_1 (
    .out_3(microcounter_1_out_3[0]), .out_4(microcounter_1_out_3[1]), .out_5(microcounter_1_out_3[2]),
    .in_1(not_1_out), .in_2(or_1_out), .out_6(microcounter_1_out_3[3]));
  not not_1 (not_1_out, clock_4_out);
  or or_1 (or_1_out, in_2, MCC);
  Clock clock_4 (.out(clock_4_out));
  LED led_22 (.in(A_r1));
  LED led_23 (.in(A_r0));
  LED led_24 (.in(A_r2));
  LED led_25 (.in(A_r3));
  LED led_26 (.in(ALU_out_27));
  LED led_27 (.in(ALU_out_25));
  LED led_28 (.in(ALU_out_24));
  LED led_29 (.in(ALU_out_26));
  LED led_30 (.in(B_r2));
  LED led_31 (.in(B_r0));
  LED led_32 (.in(B_r1));
  LED led_33 (.in(B_r3));
  Pull_Resistor pull_resistor_1 (.node(in_4));
  Pull_Resistor pull_resistor_2 (.node(in_3));
  LED led_34 (.in(microcounter_1_out_3[0]));
  LED led_35 (.in(microcounter_1_out_3[1]));
  LED led_36 (.in(microcounter_1_out_3[2]));
  LED led_37 (.in(microcounter_1_out_3[3]));
  LED led_38 (.in(in_4));
  LED led_39 (.in(in_3));
  _8_bit_register A (
    .ld(LDA), .clk(clock_2_out), .clr(in_2), .r0(A_r0), .r1(A_r1), .r2(A_r2), .r3(A_r3), .r4(A_r4),
    .r5(A_r5), .r6(A_r6), .r7(A_r7), .oe(OEA), .out_13(in_10), .out_14(in_9), .out_15(in_8), .out_16(in_7),
    .out_17(in_6), .out_18(in_5), .out_19(in_4), .out_20(in_3), .in_1(in_3), .in_2(in_4), .in_3(in_5),
    .in_4(in_6), .in_5(in_7), .in_6(in_8), .in_7(in_9), .in_8(in_10));
  _8_bit_register B (
    .ld(LDB), .clk(clock_3_out), .clr(in_2), .r0(B_r0), .r1(B_r1), .r2(B_r2), .r3(B_r3), .r4(B_r4),
    .r5(B_r5), .r6(B_r6), .r7(B_r7), .oe(OEB), .out_13(in_10), .out_14(in_9), .out_15(in_8), .out_16(in_7),
    .out_17(in_6), .out_18(in_5), .out_19(in_4), .out_20(in_3), .in_1(in_3), .in_2(in_4), .in_3(in_5),
    .in_4(in_6), .in_5(in_7), .in_6(in_8), .in_7(in_9), .in_8(in_10));
  Pull_Resistor pull_resistor_3 (.node(in_6));
  Pull_Resistor pull_resistor_4 (.node(in_5));
  LED led_40 (.in(in_8));
  LED led_41 (.in(in_7));
  LED led_42 (.in(in_5));
  LED led_43 (.in(in_6));
  LED led_44 (.in(in_9));
  LED led_45 (.in(in_10));
  Pull_Resistor pull_resistor_5 (.node(in_10));
  Pull_Resistor pull_resistor_6 (.node(in_8));
  Pull_Resistor pull_resistor_7 (.node(in_9));
  LED led_46 (.in(PC_out_14));
  LED led_47 (.in(PC_out_15));
  Clock clock_5 (.out(clock_5_out));
  LED led_48 (.in(ram_1_out_26));
  LED led_49 (.in(ram_1_out_25));
  Clock clock_6 (.out(clock_6_out));
  Pull_Resistor pull_resistor_8 (.node(in_7));
  Clock clock_7 (.out(clock_7_out));
  LED led_50 (.in(microcounter_1_out_3[6]));
  LED led_51 (.in(microcounter_1_out_3[7]));
  pc PC (
    .in_1(in_10), .in_3(in_9), .in_4(in_8), .in_5(in_7), .in_6(PCC), .out_10(in_10), .out_11(in_9),
    .out_12(in_8), .out_13(in_7), .in_2(PCLD), .in_9(in_2), .in_7(PCO), .out_17(PC_out_17),
    .out_16(PC_out_16), .out_15(PC_out_15), .out_14(PC_out_14), .in_8(clock_8_out));
  Clock clock_8 (.out(clock_8_out));
  LED led_52 (.in(PC_out_16));
  LED led_53 (.in(PC_out_17));
  LED led_54 (.in(MA_Register_r3));
  LED led_55 (.in(MA_Register_r2));
  ram ram_1 (
    .in_9(MA_Register_r0), .in_10(MA_Register_r1), .in_11(MA_Register_r2), .in_12(MA_Register_r3),
    .out_17(in_10), .out_18(in_9), .out_19(in_8), .out_20(in_7), .out_21(in_6), .out_22(in_5), .out_23(in_4),
    .out_24(in_3), .in_1(in_3), .in_2(in_4), .in_3(in_5), .in_4(in_6), .in_5(in_7), .in_6(in_8), .in_7(in_9),
    .in_8(in_10), .in_16(RAMW), .in_14(in_1), .in_13(RAMO), .in_15(clock_9_out), .out_25(ram_1_out_25),
    .out_26(ram_1_out_26), .out_27(ram_1_out_27), .out_28(ram_1_out_28), .out_29(ram_1_out_29),
    .out_30(ram_1_out_30), .out_31(ram_1_out_31), .out_32(ram_1_out_32));
  LED led_56 (.in(ram_1_out_27));
  LED led_57 (.in(ram_1_out_30));
  LED led_58 (.in(ram_1_out_29));
  LED led_59 (.in(ram_1_out_28));
  LED led_60 (.in(Current_instruction_register_r2));
  LED led_61 (.in(Current_instruction_register_r3));
  LED led_62 (.in(microcounter_1_out_3[4]));
  LED led_63 (.in(microcounter_1_out_3[5]));
  _8_bit_register MA_Register (
    .ld(MALD), .clk(clock_5_out), .clr(in_2), .r0(MA_Register_r0), .r1(MA_Register_r1), .r2(MA_Register_r2),
    .r3(MA_Register_r3), .oe(MAO), .out_13(in_10), .out_14(in_9), .out_15(in_8), .out_16(in_7),
    .out_17(MA_Register_out_17), .out_18(MA_Register_out_17), .out_19(MA_Register_out_17),
    .out_20(MA_Register_out_17), .in_1(MA_Register_out_17), .in_2(MA_Register_out_17),
    .in_3(MA_Register_out_17), .in_4(MA_Register_out_17), .in_5(in_7), .in_6(in_8), .in_7(in_9), .in_8(in_10));  // open: r4, r5, r6, r7
  LED led_64 (.in(MA_Register_r1));
  LED led_65 (.in(MA_Register_r0));
  Clock clock_9 (.out(clock_9_out));
  LED led_66 (.in(ram_1_out_32));
  LED led_67 (.in(ram_1_out_31));
  _8_bit_register u_8_bit_register_1 (
    .ld(ORLD), .clk(clock_6_out), .clr(in_2), .r0(O8), .r1(O7), .r2(O6), .r3(O5), .r4(O4), .r5(O3), .r6(O2),
    .r7(O1), .oe(1'b0), .in_1(in_3), .in_2(in_4), .in_3(in_5), .in_4(in_6), .in_5(in_7), .in_6(in_8),
    .in_7(in_9), .in_8(in_10));  // open: out_13, out_14, out_15, out_16, out_17, out_18, out_19, out_20
  _8_bit_register Current_instruction_register (
    .ld(IRLD), .clk(clock_7_out), .clr(in_2), .r0(Current_instruction_register_r0),
    .r1(Current_instruction_register_r1), .r2(Current_instruction_register_r2),
    .r3(Current_instruction_register_r3), .r4(microcounter_1_out_3[4]), .r5(microcounter_1_out_3[5]),
    .r6(microcounter_1_out_3[6]), .r7(microcounter_1_out_3[7]), .oe(IRO), .out_13(in_10), .out_14(in_9),
    .out_15(in_8), .out_16(in_7), .in_1(in_3), .in_2(in_4), .in_3(in_5), .in_4(in_6), .in_5(in_7),
    .in_6(in_8), .in_7(in_9), .in_8(in_10));  // open: out_17, out_18, out_19, out_20
  LED led_68 (.in(Current_instruction_register_r1));
  LED led_69 (.in(Current_instruction_register_r0));
  // also tied to GND on the sheet: MA_Register_out_17

  // Other names for the same wires on the sheet: CLR = in_2

  // Notes on the sheet:
  //   OR output
  //   contents of rom_1 (hex, n*v repeats v):
  //   120 12 80 1 12*0 120 12 80 24 4010 1 10*0 120 12 80 24 1010 1 10*0 120 12 80 14800 1 11*0 120 12 204
  //   1 12*0 120 12 80 14c00 1 11*0 120 12 80 1 12*0 120 12 80 28000 1 139*0 120 12 80 1 12*0 120 12 80 24
  //   4010 1 10*0 120 12 80 24 1010 1 10*0 120 12 80 14800 1 11*0 120 12 204 1 12*0 120 12 80 14c00 1 11*0
  //   120 12 204 1 12*0 120 12 80 28000 1 139*0 120 12 80 1 12*0 120 12 80 24 4010 1 10*0 120 12 80 24
  //   1010 1 10*0 120 12 80 14800 1 11*0 120 12 204 1 12*0 120 12 80 14c00 1 11*0 120 12 80 1 12*0 120 12
  //   80 28000 1 139*0 120 12 80 1 12*0 120 12 80 24 4010 1 10*0 120 12 80 24 1010 1 10*0 120 12 80 14800
  //   1 11*0 120 12 204 1 12*0 120 12 80 14c00 1 11*0 120 12 204 1 12*0 120 12 80 28000 1
  //   ALU output
  //   Contents at current address
  //   Contents of addres register
endmodule

module _8_bit_register (
  input  in_1,
  input  in_2,
  input  in_3,
  input  in_4,
  input  in_5,
  input  in_6,
  input  in_7,
  input  in_8,
  input  ld,
  input  clk,
  input  clr,
  input  oe,
  output out_13,
  output out_14,
  output out_15,
  output out_16,
  output out_17,
  output out_18,
  output out_19,
  output out_20,
  output r7,
  output r6,
  output r5,
  output r4,
  output r3,
  output r2,
  output r1,
  output r0
);

  Register register_1 (
    .D({in_1, in_2, in_3, in_4, in_5, in_6, in_7, in_8}), .en(ld), .Q({r7, r6, r5, r4, r3, r2, r1, r0}),
    .clk(clk), .clr(clr));
  assign out_13 = oe ? r0 : 1'bz;  // Controlled_Buffer controlled_buffer_1
  assign out_14 = oe ? r1 : 1'bz;  // Controlled_Buffer controlled_buffer_2
  assign out_15 = oe ? r2 : 1'bz;  // Controlled_Buffer controlled_buffer_3
  assign out_16 = oe ? r3 : 1'bz;  // Controlled_Buffer controlled_buffer_4
  assign out_17 = oe ? r4 : 1'bz;  // Controlled_Buffer controlled_buffer_5
  assign out_18 = oe ? r5 : 1'bz;  // Controlled_Buffer controlled_buffer_6
  assign out_19 = oe ? r6 : 1'bz;  // Controlled_Buffer controlled_buffer_7
  assign out_20 = oe ? r7 : 1'bz;  // Controlled_Buffer controlled_buffer_8
endmodule

module alu (
  input  in_1,
  input  in_2,
  input  in_3,
  input  in_4,
  input  in_5,
  input  in_6,
  input  in_7,
  input  in_8,
  input  in_9,
  input  in_10,
  input  in_11,
  input  in_12,
  input  in_13,
  input  in_14,
  input  in_15,
  input  in_16,
  input  in_17,
  input  in_18,
  output out_19,
  output out_20,
  output out_21,
  output out_22,
  output out_23,
  output out_24,
  output out_25,
  output out_26,
  output out_27,
  output out_28,
  output out_29,
  output out_30,
  output out_31,
  output out_32,
  output out_33,
  output out_34,
  output out_35,
  output out_36,
  output out_37
);

  wire and_1_out, xnor_1_out;
  wire [7:0] adder_1_out, subtractor_1_out;

  Adder adder_1 (
    .a({in_8, in_7, in_6, in_5, in_4, in_3, in_2, in_1}),
    .b({in_18, in_16, in_15, in_14, in_13, in_12, in_10, in_9}), .out(adder_1_out), .cin(1'b0), .cout(out_36));
  Subtractor subtractor_1 (
    .a({in_8, in_7, in_6, in_5, in_4, in_3, in_2, in_1}),
    .b({in_18, in_16, in_15, in_14, in_13, in_12, in_10, in_9}), .out(subtractor_1_out), .bin(1'b0),
    .bout(out_37));
  xnor xnor_1 (xnor_1_out, 1'b0, in_17);
  and and_1 (and_1_out, in_17, 1'b1);
  assign out_27 = xnor_1_out ? adder_1_out[0] : 1'bz;  // Controlled_Buffer controlled_buffer_1
  assign out_26 = xnor_1_out ? adder_1_out[1] : 1'bz;  // Controlled_Buffer controlled_buffer_2
  assign out_25 = xnor_1_out ? adder_1_out[2] : 1'bz;  // Controlled_Buffer controlled_buffer_3
  assign out_24 = xnor_1_out ? adder_1_out[3] : 1'bz;  // Controlled_Buffer controlled_buffer_4
  assign out_23 = xnor_1_out ? adder_1_out[4] : 1'bz;  // Controlled_Buffer controlled_buffer_5
  assign out_22 = xnor_1_out ? adder_1_out[5] : 1'bz;  // Controlled_Buffer controlled_buffer_6
  assign out_21 = xnor_1_out ? adder_1_out[6] : 1'bz;  // Controlled_Buffer controlled_buffer_7
  assign out_20 = xnor_1_out ? adder_1_out[7] : 1'bz;  // Controlled_Buffer controlled_buffer_8
  assign out_27 = and_1_out ? subtractor_1_out[0] : 1'bz;  // Controlled_Buffer controlled_buffer_9
  assign out_26 = and_1_out ? subtractor_1_out[1] : 1'bz;  // Controlled_Buffer controlled_buffer_10
  assign out_25 = and_1_out ? subtractor_1_out[2] : 1'bz;  // Controlled_Buffer controlled_buffer_11
  assign out_24 = and_1_out ? subtractor_1_out[3] : 1'bz;  // Controlled_Buffer controlled_buffer_12
  assign out_23 = and_1_out ? subtractor_1_out[4] : 1'bz;  // Controlled_Buffer controlled_buffer_13
  assign out_22 = and_1_out ? subtractor_1_out[5] : 1'bz;  // Controlled_Buffer controlled_buffer_14
  assign out_21 = and_1_out ? subtractor_1_out[6] : 1'bz;  // Controlled_Buffer controlled_buffer_15
  assign out_20 = and_1_out ? subtractor_1_out[7] : 1'bz;  // Controlled_Buffer controlled_buffer_16
  nor nor_1 (out_19, out_20, out_21, out_22, out_23, out_24, out_25, out_26, out_27);
  assign out_28 = in_11 ? out_27 : 1'bz;  // Controlled_Buffer controlled_buffer_17
  assign out_29 = in_11 ? out_26 : 1'bz;  // Controlled_Buffer controlled_buffer_18
  assign out_30 = in_11 ? out_25 : 1'bz;  // Controlled_Buffer controlled_buffer_19
  assign out_31 = in_11 ? out_24 : 1'bz;  // Controlled_Buffer controlled_buffer_20
  assign out_32 = in_11 ? out_23 : 1'bz;  // Controlled_Buffer controlled_buffer_21
  assign out_33 = in_11 ? out_22 : 1'bz;  // Controlled_Buffer controlled_buffer_22
  assign out_34 = in_11 ? out_21 : 1'bz;  // Controlled_Buffer controlled_buffer_23
  assign out_35 = in_11 ? out_20 : 1'bz;  // Controlled_Buffer controlled_buffer_24
endmodule

module ram (
  input  in_1,
  input  in_2,
  input  in_3,
  input  in_4,
  input  in_5,
  input  in_6,
  input  in_7,
  input  in_8,
  input  in_9,
  input  in_10,
  input  in_11,
  input  in_12,
  input  in_13,
  input  in_14,
  input  in_15,
  input  in_16,
  output out_17,
  output out_18,
  output out_19,
  output out_20,
  output out_21,
  output out_22,
  output out_23,
  output out_24,
  output out_25,
  output out_26,
  output out_27,
  output out_28,
  output out_29,
  output out_30,
  output out_31,
  output out_32
);

  wire not_1_out, not_2_out;

  not not_1 (not_1_out, in_16);
  RAM #(.addrWidth(4)) ram_1 (
    .addr({in_12, in_11, in_10, in_9}),
    .data({out_25, out_26, out_27, out_28, out_29, out_30, out_31, out_32}), .sel(1'b1), .clk(in_15),
    .ld(not_1_out), .clr(in_14));
  not not_2 (not_2_out, not_1_out);
  assign out_25 = not_2_out ? in_1 : 1'bz;  // Controlled_Buffer controlled_buffer_1
  assign out_28 = not_2_out ? in_4 : 1'bz;  // Controlled_Buffer controlled_buffer_2
  assign out_27 = not_2_out ? in_3 : 1'bz;  // Controlled_Buffer controlled_buffer_3
  assign out_26 = not_2_out ? in_2 : 1'bz;  // Controlled_Buffer controlled_buffer_4
  assign out_30 = not_2_out ? in_6 : 1'bz;  // Controlled_Buffer controlled_buffer_5
  assign out_31 = not_2_out ? in_7 : 1'bz;  // Controlled_Buffer controlled_buffer_6
  assign out_32 = not_2_out ? in_8 : 1'bz;  // Controlled_Buffer controlled_buffer_7
  assign out_29 = not_2_out ? in_5 : 1'bz;  // Controlled_Buffer controlled_buffer_8
  assign out_17 = in_13 ? out_32 : 1'bz;  // Controlled_Buffer controlled_buffer_9
  assign out_18 = in_13 ? out_31 : 1'bz;  // Controlled_Buffer controlled_buffer_10
  assign out_19 = in_13 ? out_30 : 1'bz;  // Controlled_Buffer controlled_buffer_11
  assign out_20 = in_13 ? out_29 : 1'bz;  // Controlled_Buffer controlled_buffer_12
  assign out_21 = in_13 ? out_28 : 1'bz;  // Controlled_Buffer controlled_buffer_13
  assign out_22 = in_13 ? out_27 : 1'bz;  // Controlled_Buffer controlled_buffer_14
  assign out_23 = in_13 ? out_26 : 1'bz;  // Controlled_Buffer controlled_buffer_15
  assign out_24 = in_13 ? out_25 : 1'bz;  // Controlled_Buffer controlled_buffer_16
endmodule

module pc (
  input  in_1,
  input  in_2,
  input  in_3,
  input  in_4,
  input  in_5,
  input  in_6,
  input  in_7,
  input  in_8,
  input  in_9,
  output out_10,
  output out_11,
  output out_12,
  output out_13,
  output out_14,
  output out_15,
  output out_16,
  output out_17
);

  Counter #(.width(4), .max('hf)) counter_1 (
    .load(in_2), .D({in_5, in_4, in_3, in_1}), .count(in_6), .Q({out_14, out_15, out_16, out_17}),
    .clk(in_8), .clr(in_9));  // open: carry
  assign out_10 = in_7 ? out_17 : 1'bz;  // Controlled_Buffer controlled_buffer_1
  assign out_11 = in_7 ? out_16 : 1'bz;  // Controlled_Buffer controlled_buffer_2
  assign out_12 = in_7 ? out_15 : 1'bz;  // Controlled_Buffer controlled_buffer_3
  assign out_13 = in_7 ? out_14 : 1'bz;  // Controlled_Buffer controlled_buffer_4
endmodule

module microcounter (
  input  in_1,
  input  in_2,
  output out_3,
  output out_4,
  output out_5,
  output out_6
);

  Counter #(.width(4), .max('hf)) counter_1 (
    .load(1'b0), .count(1'b1), .Q({out_6, out_5, out_4, out_3}), .clk(in_1), .clr(in_2));  // open: D, carry
endmodule
