// Logisim project register.circ as structural Verilog
module _8_bit_register (
  input  b0,
  input  b1,
  input  b2,
  input  b3,
  input  b4,
  input  b5,
  input  b6,
  input  b7,
  input  ld,
  input  clk,
  input  clr,
  input  oe,
  output r0,
  output r1,
  output r2,
  output r3,
  output r4,
  output r5,
  output r6,
  output r7
);

  Register register_1 (
    .D({b7, b6, b5, b4, b3, b2, b1, b0}), .en(ld), .Q({r7, r6, r5, r4, r3, r2, r1, r0}), .clk(clk), .clr(clr));
  assign b0 = oe ? r0 : 1'bz;  // Controlled_Buffer controlled_buffer_1
  assign b1 = oe ? r1 : 1'bz;  // Controlled_Buffer controlled_buffer_2
  assign b2 = oe ? r2 : 1'bz;  // Controlled_Buffer controlled_buffer_3
  assign b3 = oe ? r3 : 1'bz;  // Controlled_Buffer controlled_buffer_4
  assign b4 = oe ? r4 : 1'bz;  // Controlled_Buffer controlled_buffer_5
  assign b5 = oe ? r5 : 1'bz;  // Controlled_Buffer controlled_buffer_6
  assign b6 = oe ? r6 : 1'bz;  // Controlled_Buffer controlled_buffer_7
  assign b7 = oe ? r7 : 1'bz;  // Controlled_Buffer controlled_buffer_8
endmodule
